# Fritzing sketch Strobe V1.0 routed with groundfill (saved by Fritzing 0.9.3b)
circuit board: 3.15596cm x 3.50712cm
breadboards: 1

parts:
  U1 = attiny85 [package=dip]
  S1 = Momentary Switch [package=tactile-pth]
  R1 = Resistor [tolerance=±5% resistance=100 package="0805 [SMD]"]
  R2 = Resistor [tolerance=±5% resistance=100 package="0805 [SMD]"]
  WING = Header 3 [package=screwterminal-3.5mm-3_lock.007s]
  WING_2 = Header 3 [package=screwterminal-3.5mm-3_lock.007s]
  7805 = Voltage Regulator - 5V [package="DPak [SMD]"]
  C1 = Electrolytic Capacitor [capacitance=47µF voltage=20V package="100 mil [THT, electrolytic]"]
  C2 = Electrolytic Capacitor [capacitance=47µF voltage=20V package="100 mil [THT, electrolytic]"]
  Q2 = NPN-Transistor [package="TO92 [THT]"]
  BATT = Header 2 [package=screwterminal-3.5mm-2_lock]
  R6 = Resistor [tolerance=±5% resistance=2.2k package="0805 [SMD]"]
  Q1 = NPN-Transistor [package="TO92 [THT]"]
  BCN = Header 2 [package=screwterminal-3.5mm-2_lock]
  R7 = Resistor [tolerance=±5% resistance=100 package="0805 [SMD]"]
  R8 = Resistor [tolerance=±5% resistance=10k package="0805 [SMD]"]
  R9 = Resistor [tolerance=±5% resistance=100 package="0805 [SMD]"]
  R2_2 = Resistor [tolerance=±5% resistance=100 package="0805 [SMD]"]
  R3 = Resistor [tolerance=±1% resistance=4.7k package="0805 [SMD]"]
  AUX = female pin header, 2 pins [form="♀ (female)"]

nets:
  GND: U1.Pin_4, 7805.GND, C1.-, C2.-, Q2.C, BATT.1, Q1.C, R8.Pin_1, R9.Pin_1, R2_2.Pin_1, AUX.pin1
  N1: U1.Pin_5, R6.Pin_0
  N2: U1.Pin_6, R3.Pin_1
  N3: U1.Pin_7, S1.4, R8.Pin_0
  VCC: U1.Pin_8, S1.1, WING.1, WING_2.1, 7805.output_voltage, C2.+, BCN.2, AUX.pin2
  N4: R1.Pin_0, R2.Pin_0, Q2.E
  N5: R1.Pin_1, WING.3
  N6: R2.Pin_1, WING_2.3
  N7: WING.2, R9.Pin_0
  N8: WING_2.2, R2_2.Pin_0
  N9: 7805.input_voltage, C1.+, BATT.2
  N10: Q2.B, R3.Pin_0
  N11: R6.Pin_1, Q1.B
  N12: Q1.E, R7.Pin_0
  N13: BCN.1, R7.Pin_1

notes:
  +
  L
  S
  -
  UAV Strobe    V1.0
  www.mkme.org

custom parts:
  NPN-Transistor: A standard NPN-transistor
